# Fritzing sketch Power_Diagram (saved by Fritzing 0.9.3b)

parts:
  U1 = ESP32-38PinWide [part_number=ESP32-38PinWide]
  o1 = Module display OLED I2C 128x64 SSD1306 [package=THT]
  M1 = MakerFocus MAX30102

nets:
  N1: U1.GPIO13, M1.INT
  GND: U1.GPIO11, o1.GND, M1.GND
  VIN: U1.VIN, o1.VCC
  N2: U1.GPIO22, o1.SCL, M1.SCL
  N3: o1.SDA, M1.SDA

notes:
  ESP32 -WROOM
  MAX30102 ESP32 OLED
  -----------------------------------------------------
  GND | GND | GND
  VIN | 3.3V | VIN
  SCL | 22 | SCL
  SDA | 21 | SDA
  INT | 13 |

custom parts:
  ESP32-38PinWide: Generic 38-Pin ESP32 with wide format (only access to one side of pins on a breadboard) based on Stephen Lilley's HiLetgo ESP-WROOM-32 ESP32 ESP-32S Development Board.
  Module display OLED I2C 128x64 SSD1306: Ecran OLED I2C SSD163 de 128x64 avec connexion I2C
  MakerFocus MAX30102: Oximeter module using the MAX30102 chip. As usual, if you want the mounting holes in pcb, you need to drag a hole over the pad in silkscreen to actually drill the hole (by default they are not drilled)
